// Logisim project product.circ as structural Verilog: 2 circuits, main circuit product
module product (
  input  [3:0] a,
  input  [3:0] b,
  output [7:0] product
);

  wire and_1_out, and_2_out, and_3_out, and_4_out, and_5_out, and_6_out, and_7_out, and_8_out, and_9_out,
       and_10_out, and_11_out, and_12_out, and_13_out, and_14_out, and_15_out, and_16_out;

  and and_1 (and_1_out, b[3], a[3]);
  and and_2 (and_2_out, b[3], a[2]);
  and and_3 (and_3_out, b[2], a[3]);
  and and_4 (and_4_out, b[3], a[1]);
  and and_5 (and_5_out, b[2], a[2]);
  and and_6 (and_6_out, b[1], a[3]);
  and and_7 (and_7_out, b[3], a[0]);
  and and_8 (and_8_out, b[2], a[0]);
  and and_9 (and_9_out, b[2], a[1]);
  and and_10 (and_10_out, b[1], a[2]);
  and and_11 (and_11_out, b[0], a[3]);
  and and_12 (and_12_out, b[1], a[0]);
  and and_13 (and_13_out, b[1], a[1]);
  and and_14 (and_14_out, b[0], a[2]);
  and and_15 (and_15_out, b[0], a[0]);
  and and_16 (and_16_out, b[0], a[1]);
  carry_save_adder CARRY_SAVE_ADDER (
    .D6(and_1_out), .D5(and_3_out), .C5(and_2_out), .D4(and_6_out), .C4(and_5_out), .B4(and_4_out),
    .D3(and_11_out), .C3(and_10_out), .B3(and_9_out), .A3(and_7_out), .C2(and_14_out), .B2(and_13_out),
    .A2(and_8_out), .B1(and_12_out), .A1(and_16_out), .A0(and_15_out), .S7(product[7]), .S6(product[6]),
    .S5(product[5]), .S4(product[4]), .S3(product[3]), .S2(product[2]), .S1(product[1]), .S0(product[0]));
endmodule

module carry_save_adder (
  input  B1,
  input  A1,
  input  A0,
  input  D6,
  input  D5,
  input  C5,
  input  D4,
  input  C4,
  input  B4,
  input  D3,
  input  C3,
  input  B3,
  input  A3,
  input  C2,
  input  B2,
  input  A2,
  output S7,
  output S6,
  output S5,
  output S4,
  output S3,
  output S2,
  output S1,
  output S0
);

  wire adder_2_cout, adder_2_out, adder_3_cout, adder_4_cout, adder_4_out, adder_5_cout, adder_5_out,
       adder_6_cout, adder_7_cout, adder_7_out, adder_8_cout, adder_8_out, adder_9_cout, adder_10_cout,
       adder_10_out, adder_11_cout, adder_12_cout;

  Adder #(.width(1)) adder_1 (.a(D6), .b(adder_2_cout), .out(S6), .cin(adder_3_cout), .cout(S7));
  Adder #(.width(1)) adder_2 (.a(C5), .b(D5), .out(adder_2_out), .cin(adder_5_cout), .cout(adder_2_cout));
  Adder #(.width(1)) adder_3 (.a(adder_4_cout), .b(adder_6_cout), .out(S5), .cin(adder_2_out), .cout(adder_3_cout));
  Adder #(.width(1)) adder_4 (.a(B4), .b(C4), .out(adder_4_out), .cin(adder_7_cout), .cout(adder_4_cout));
  Adder #(.width(1)) adder_5 (.a(adder_4_out), .b(D4), .out(adder_5_out), .cin(adder_8_cout), .cout(adder_5_cout));
  Adder #(.width(1)) adder_6 (.a(adder_5_out), .b(1'b0), .out(S4), .cin(adder_9_cout), .cout(adder_6_cout));
  Adder #(.width(1)) adder_7 (.a(A3), .b(B3), .out(adder_7_out), .cout(adder_7_cout));  // open: cin
  Adder #(.width(1)) adder_8 (.a(adder_7_out), .b(C3), .out(adder_8_out), .cin(adder_10_cout), .cout(adder_8_cout));
  Adder #(.width(1)) adder_9 (.a(adder_8_out), .b(D3), .out(S3), .cin(adder_11_cout), .cout(adder_9_cout));
  Adder #(.width(1)) adder_10 (.a(A2), .b(B2), .out(adder_10_out), .cout(adder_10_cout));  // open: cin
  Adder #(.width(1)) adder_11 (.a(adder_10_out), .b(C2), .out(S2), .cin(adder_12_cout), .cout(adder_11_cout));
  Adder #(.width(1)) adder_12 (.a(A1), .b(B1), .out(S1), .cout(adder_12_cout));  // open: cin

  assign S0 = A0;
endmodule
